// Logisim project PIC8.circ as structural Verilog: 6 circuits, main circuit main
module main (
);

  wire CLK, not_1_out, regbank_1_write_ram, RST;
  wire [7:0] multiplexer_1_out, regbank_1_endereco_ram, regbank_1_input_ram;

  regBank regbank_1 (
    .clock(CLK), .reset(RST), .output_ram(multiplexer_1_out), .write_ram(regbank_1_write_ram),
    .input_ram(regbank_1_input_ram), .endereco_ram(regbank_1_endereco_ram));  // open: data_in, write_data, endereco_in, endereco_out, data_out, port_a, port_b, work_out
  Multiplexer #(.width(8), .enable("false")) multiplexer_1 (
    .in1(regbank_1_input_ram), .out(multiplexer_1_out), .sel(regbank_1_write_ram));  // open: in0
  RAM ram_1 (
    .addr(regbank_1_endereco_ram), .we(regbank_1_write_ram), .oe(not_1_out), .clk(CLK),
    .data(multiplexer_1_out));
  not not_1 (not_1_out, regbank_1_write_ram);
endmodule

module reg8bits (
  input  [7:0] data_in,
  input  enable,
  input  clock,
  input  reset,
  output [7:0] data_out
);

  wire and_1_out, and_2_out, and_3_out, and_4_out, and_5_out, and_6_out, and_7_out, and_8_out;

  and and_1 (and_1_out, enable, clock);
  and and_2 (and_2_out, enable, clock);
  and and_3 (and_3_out, enable, clock);
  and and_4 (and_4_out, enable, clock);
  and and_5 (and_5_out, enable, clock);
  and and_6 (and_6_out, enable, clock);
  and and_7 (and_7_out, enable, clock);
  and and_8 (and_8_out, enable, clock);
  D_Flip_Flop d_ff_1 (.D(data_in[0]), .clk(and_1_out), .Q(data_out[0]), .reset(reset));  // open: Qn, preset
  D_Flip_Flop d_ff_2 (.D(data_in[1]), .clk(and_2_out), .Q(data_out[1]), .reset(reset));  // open: Qn, preset
  D_Flip_Flop d_ff_3 (.D(data_in[2]), .clk(and_3_out), .Q(data_out[2]), .reset(reset));  // open: Qn, preset
  D_Flip_Flop d_ff_4 (.D(data_in[3]), .clk(and_4_out), .Q(data_out[3]), .reset(reset));  // open: Qn, preset
  D_Flip_Flop d_ff_5 (.D(data_in[4]), .clk(and_5_out), .Q(data_out[4]), .reset(reset));  // open: Qn, preset
  D_Flip_Flop d_ff_6 (.D(data_in[5]), .clk(and_6_out), .Q(data_out[5]), .reset(reset));  // open: Qn, preset
  D_Flip_Flop d_ff_7 (.D(data_in[6]), .clk(and_7_out), .Q(data_out[6]), .reset(reset));  // open: Qn, preset
  D_Flip_Flop d_ff_8 (.D(data_in[7]), .clk(and_8_out), .Q(data_out[7]), .reset(reset));  // open: Qn, preset

  // Other names for the same wires on the sheet: CLK = clock; D0 = data_in[0]; D1 = data_in[1]; D2 = data_in[2];
  //   D3 = data_in[3]; D4 = data_in[4]; D5 = data_in[5]; D6 = data_in[6]; D7 = data_in[7]; ENB = enable; RST = reset
endmodule

module regBank (
  input  [7:0] data_in,
  input  write_data,
  input  [5:0] endereco_in,
  input  [5:0] endereco_out,
  input  clock,
  input  reset,
  input  [7:0] output_ram,
  output [7:0] data_out,
  output write_ram,
  output [7:0] input_ram,
  output [7:0] endereco_ram,
  output [7:0] port_a,
  output [7:0] port_b,
  output [7:0] work_out
);

  wire demultiplexer_1_out0, demultiplexer_1_out1, fsr, portA, portB, s1, s2, s3, s4, s5, s6, s7, s8, s9,
       s10, s11, s12, s13, s14, s15, s16, status, trisA, trisB, work;
  wire [7:0] multiplexer_1_out, multiplexer_2_out, outS1, outS2, outS3, outS4, outS5, outS6, outS7, outS8,
       outS9, outS10, outS11, outS12, outS13, outS14, outS15, outS16, outStatus, outTrisA, outTrisB;

  Demultiplexer #(.enable("false")) demultiplexer_1 (
    .out0(demultiplexer_1_out0), .out1(demultiplexer_1_out1), .in(write_data), .sel(endereco_in[5]));
  Demultiplexer #(.select(5), .enable("false")) demultiplexer_2 (
    .out1(fsr), .out2(trisA), .out3(trisB), .out4(portA), .out5(portB), .out6(s1), .out7(s2), .out8(s3),
    .out9(s4), .out10(s5), .out11(s6), .out12(s7), .out13(s8), .out14(s9), .out15(s10), .out16(s11),
    .out17(s12), .out18(s13), .out19(s14), .out20(s15), .out21(s16), .in(demultiplexer_1_out0),
    .sel(endereco_in[4:0]));  // open: out0, out22, out23, out24, out25, out26, out27, out28, out29, out30, out31
  Demultiplexer #(.select(5), .enable("false")) demultiplexer_3 (
    .out29(status), .out30(write_ram), .out31(work), .in(demultiplexer_1_out1), .sel(endereco_in[4:0]));  // open: out0, out1, out2, out3, out4, out5, out6, out7, out8, out9, out10, out11, out12, out13, out14, out15, out16, out17, out18, out19, out20, out21, out22, out23, out24, out25, out26, out27, out28
  reg8bits u_FSR (.data_in(data_in), .enable(fsr), .clock(clock), .reset(reset), .data_out(endereco_ram));
  // Probe on endereco_ram
  reg8bits u_TRISA (.data_in(data_in), .enable(trisA), .clock(clock), .reset(reset), .data_out(outTrisA));
  // Probe on outTrisA
  reg8bits u_TRISB (.data_in(data_in), .enable(trisB), .clock(clock), .reset(reset), .data_out(outTrisB));
  // Probe on outTrisB
  reg8bits u_PORTA (.data_in(data_in), .enable(portA), .clock(clock), .reset(reset), .data_out(port_a));
  // Probe on port_a
  reg8bits u_PORTB (.data_in(data_in), .enable(portB), .clock(clock), .reset(reset), .data_out(port_b));
  // Probe on port_b
  reg8bits u_STATUS (.data_in(data_in), .enable(status), .clock(clock), .reset(reset), .data_out(outStatus));
  // Probe on outStatus
  reg8bits u_WORK (.data_in(data_in), .enable(work), .clock(clock), .reset(reset), .data_out(work_out));
  // Probe on work_out
  reg8bits u_S1 (.data_in(data_in), .enable(s1), .clock(clock), .reset(reset), .data_out(outS1));
  // Probe on outS1
  reg8bits u_S2 (.data_in(data_in), .enable(s2), .clock(clock), .reset(reset), .data_out(outS2));
  // Probe on outS2
  reg8bits u_S3 (.data_in(data_in), .enable(s3), .clock(clock), .reset(reset), .data_out(outS3));
  // Probe on outS3
  reg8bits u_S4 (.data_in(data_in), .enable(s4), .clock(clock), .reset(reset), .data_out(outS4));
  // Probe on outS4
  reg8bits u_S5 (.data_in(data_in), .enable(s5), .clock(clock), .reset(reset), .data_out(outS5));
  // Probe on outS5
  reg8bits u_S6 (.data_in(data_in), .enable(s6), .clock(clock), .reset(reset), .data_out(outS6));
  // Probe on outS6
  reg8bits u_S7 (.data_in(data_in), .enable(s7), .clock(clock), .reset(reset), .data_out(outS7));
  // Probe on outS7
  Multiplexer #(.select(5), .width(8), .enable("false")) multiplexer_1 (
    .in0({8{1'b0}}), .in1(endereco_ram), .in2(outTrisA), .in3(outTrisB), .in4(port_a), .in5(port_b),
    .in6(outS1), .in7(outS2), .in8(outS3), .in9(outS4), .in10(outS5), .in11(outS6), .in12(outS7),
    .in13(outS8), .in14(outS9), .in15(outS10), .in16(outS11), .in17(outS12), .in18(outS13), .in19(outS14),
    .in20(outS15), .in21(outS16), .out(multiplexer_1_out), .sel(endereco_out[4:0]));  // open: in22, in23, in24, in25, in26, in27, in28, in29, in30, in31
  Multiplexer #(.select(5), .width(8), .enable("false")) multiplexer_2 (
    .in29(outStatus), .in30(output_ram), .in31(work_out), .out(multiplexer_2_out), .sel(endereco_out[4:0]));  // open: in0, in1, in2, in3, in4, in5, in6, in7, in8, in9, in10, in11, in12, in13, in14, in15, in16, in17, in18, in19, in20, in21, in22, in23, in24, in25, in26, in27, in28
  reg8bits u_S8 (.data_in(data_in), .enable(s8), .clock(clock), .reset(reset), .data_out(outS8));
  reg8bits u_S9 (.data_in(data_in), .enable(s9), .clock(clock), .reset(reset), .data_out(outS9));
  reg8bits u_S10 (.data_in(data_in), .enable(s10), .clock(clock), .reset(reset), .data_out(outS10));
  reg8bits u_S11 (.data_in(data_in), .enable(s11), .clock(clock), .reset(reset), .data_out(outS11));
  reg8bits u_S12 (.data_in(data_in), .enable(s12), .clock(clock), .reset(reset), .data_out(outS12));
  reg8bits u_S13 (.data_in(data_in), .enable(s13), .clock(clock), .reset(reset), .data_out(outS13));
  reg8bits u_S14 (.data_in(data_in), .enable(s14), .clock(clock), .reset(reset), .data_out(outS14));
  Multiplexer #(.width(8), .enable("false")) multiplexer_3 (
    .in0(multiplexer_1_out), .in1(multiplexer_2_out), .out(data_out), .sel(endereco_out[5]));
  // Probe on outS8
  // Probe on outS9
  // Probe on outS10
  // Probe on outS11
  // Probe on outS12
  // Probe on outS13
  // Probe on outS14
  reg8bits u_S15 (.data_in(data_in), .enable(s15), .clock(clock), .reset(reset), .data_out(outS15));
  // Probe on outS15
  reg8bits u_S16 (.data_in(data_in), .enable(s16), .clock(clock), .reset(reset), .data_out(outS16));
  // Probe on outS16

  assign input_ram = data_in;

  // Other names for the same wires on the sheet: clk = clock; dt[7:0] = data_in; indf = write_ram;
  //   outFsr[7:0] = endereco_ram; outPortA[7:0] = port_a; outPortB[7:0] = port_b; outWork[7:0] = work_out;
  //   rst = reset
endmodule

module reg8bits_test (
  input  in_1
);

  wire clock_1_out;
  wire [7:0] counter_1_q, reg8bits_1_data_out;

  Counter counter_1 (.clr(in_1), .up(1'b1), .clk(clock_1_out), .Q(counter_1_q));  // open: load, count, D, carry
  Clock clock_1 (.out(clock_1_out));
  // Probe on counter_1_q
  reg8bits reg8bits_1 (
    .data_in(counter_1_q), .enable(1'b1), .clock(clock_1_out), .data_out(reg8bits_1_data_out));  // open: reset
  // Probe on reg8bits_1_data_out
endmodule

module regBank_test (
  input  in_1,
  input  in_2
);

  wire clock_1_out, or_1_out;
  wire [5:0] counter_1_q;
  wire [7:0] regbank_1_data_out;
  wire [7:6] counter_1_q_2;

  or or_1 (or_1_out, counter_1_q_2[6], in_2);
  Clock clock_1 (.out(clock_1_out));
  Counter counter_1 (
    .clr(or_1_out), .up(1'b1), .clk(clock_1_out), .Q({counter_1_q_2, counter_1_q}));  // open: load, count, D, carry
  // Probe on {counter_1_q_2, counter_1_q}
  // Probe on counter_1_q
  regBank regbank_1 (
    .data_in({counter_1_q_2, counter_1_q}), .write_data(in_1), .endereco_in(counter_1_q),
    .endereco_out(counter_1_q), .clock(clock_1_out), .data_out(regbank_1_data_out));  // open: reset, output_ram, write_ram, input_ram, endereco_ram, port_a, port_b, work_out
  // Probe on regbank_1_data_out
endmodule

module ram_test (
  input  [5:0] in_1,
  input  [5:0] in_2,
  input  in_3,
  input  in_4,
  input  [5:0] in_5
);

  wire clock_1_out, demultiplexer_1_out0, demultiplexer_1_out1, multiplexer_2_out, not_1_out, not_2_out,
       or_1_out, regbank_1_write_ram;
  wire [5:0] multiplexer_1_out;
  wire [7:0] counter_1_q, multiplexer_3_out, regbank_1_data_out, regbank_1_endereco_ram, regbank_1_input_ram;

  Clock clock_1 (.out(clock_1_out));
  or or_1 (or_1_out, counter_1_q[5], in_4);
  Counter counter_1 (.clr(or_1_out), .up(1'b1), .clk(clock_1_out), .Q(counter_1_q));  // open: load, count, D, carry
  Multiplexer #(.width(6), .enable("false")) multiplexer_1 (
    .in0(in_1), .in1(in_2), .out(multiplexer_1_out), .sel(multiplexer_2_out));
  Multiplexer #(.enable("false")) multiplexer_2 (
    .in0(not_1_out), .in1(demultiplexer_1_out1), .out(multiplexer_2_out), .sel(in_3));
  not not_1 (not_1_out, demultiplexer_1_out0);
  Demultiplexer #(.enable("false")) demultiplexer_1 (
    .out0(demultiplexer_1_out0), .out1(demultiplexer_1_out1), .in(counter_1_q[0]), .sel(in_3));
  regBank regbank_1 (
    .data_in(counter_1_q), .write_data(1'b1), .endereco_in(multiplexer_1_out), .endereco_out(in_5),
    .clock(clock_1_out), .output_ram(multiplexer_3_out), .data_out(regbank_1_data_out),
    .write_ram(regbank_1_write_ram), .input_ram(regbank_1_input_ram), .endereco_ram(regbank_1_endereco_ram));  // open: reset, port_a, port_b, work_out
  // Probe on regbank_1_data_out
  Multiplexer #(.width(8), .enable("false")) multiplexer_3 (
    .in1(regbank_1_input_ram), .out(multiplexer_3_out), .sel(regbank_1_write_ram));  // open: in0
  RAM ram_1 (
    .addr(regbank_1_endereco_ram), .we(regbank_1_write_ram), .oe(not_2_out), .clk(clock_1_out),
    .data(multiplexer_3_out));
  not not_2 (not_2_out, regbank_1_write_ram);
  // Probe on multiplexer_3_out
endmodule
